# Fritzing sketch Bluetooth_car (saved by Fritzing 0.9.2b)

parts:
  Part1 = Arduino Uno (Rev3)  # not connected
  M1 = DC Motor
  Part3 = Bluetooth HC-06
  Part4 = Rotoshield - Motor driver shield for Arduino
  M2 = DC Motor

nets:
  N1: M1.pin_1, Part4.M2-1
  N2: M1.pin_2, Part4.M2-2
  N3: Part3.RXD, Part4.DIG_0
  N4: Part3.TXD, Part4.DIG_1
  GND: Part3.GND, Part4.GND
  VCC: Part3.VCC, Part4.+5V
  N5: Part4.M1-2, M2.pin_2
  N6: Part4.M1-1, M2.pin_1

// code stored in the sketch: arduino_bluetooh_car.ino
/*Autor: Jutair Rios*/
/*Projeto de um carrinho controlado por bluetooh utilizando a porta serial*/
/*A project of a car controlled by bluetooh through serial port*/

#include <AFMotor.h>
AF_DCMotor motor1(1, MOTOR12_64KHZ);
AF_DCMotor motor2(2, MOTOR12_64KHZ);;
void setup() {
Serial.begin(9600); // set serial speed
motor1.setSpeed(255);
motor2.setSpeed(255);

}


void loop(){
while (Serial.available() == 0); // do nothing if nothing sent
int val = Serial.read() - '0'; // deduct ascii value of '0' to find numeric value of sent number

if (val == 1) { // 
Serial.println("Motor Frente");
drive_frente();
Serial.flush(); 
}
else if (val == 3)//
{
Serial.println("Para");
direita();
Serial.flush(); 
}
if (val == 2) { // 
Serial.println("Motor Volta");
drive_re();
Serial.flush(); 
}

if (val == 4) { //
Serial.println("Motor Volta");
esquerda();
Serial.flush(); 
}

if (val == 5) { //
Serial.println("Motor Volta");
drive_stop();
Serial.flush(); 
}
else // if not one of above command, do nothing
{
//val = val;
}
Serial.println(val);
Serial.flush(); // clear serial port
}
void drive_frente(){              //função drive_frente
  motor1.run(FORWARD);
  motor2.run(FORWARD);
}
void drive_re(){                  //função drive_re
  motor1.run(BACKWARD);
  motor2.run(BACKWARD);
}
void drive_stop(){                //função drive_stop
 motor1.run(RELEASE); 
 motor2.run(RELEASE); 
}

void direita(){
  motor1.run(RELEASE);
  motor2.run(FORWARD);
}
void esquerda(){
   motor1.run(FORWARD);
  motor2.run(RELEASE);
}
